# Fritzing sketch Schaltung (saved by Fritzing 0.9.0b)
breadboards: 1
perfboards: 1

parts:
  R1 = Resistor [tolerance=±5% resistance=220 package=THT]
  R2 = Resistor [tolerance=±5% resistance=220 package=THT]
  R3 = Resistor [tolerance=±5% resistance=220 package=THT]
  LED1 = LED - 5mm [color="Red (633nm)" package="5 mm [THT]"]
  LED3 = LED - 5mm [color="Yellow (585nm)" package="5 mm [THT]"]
  R4 = Resistor [tolerance=±5% resistance=1M package=THT]
  Alps_Motor-Slider = DC Motor
  R5 = Slide Potentiometer [maximum_resistance=10kΩ]
  LED2 = LED - 5mm [color="Green (560nm)" package="5 mm [THT]"]
  Bauteil2 = Arduino Motor Shield (Rev3)
  Power_plug1 = Power plug

nets:
  GND: R1.Pin_0, R2.Pin_0, R3.Pin_0, R5.leg2, Bauteil2.GND, Power_plug1.GND
  N1: R1.Pin_1, LED1.cathode
  N2: R2.Pin_1, LED2.cathode
  N3: R3.Pin_1, LED3.cathode
  N4: LED1.anode, Bauteil2.A3
  N5: LED3.anode, Bauteil2.A4
  N6: R4.Pin_0, Bauteil2.D10_PWM
  N7: R4.Pin_1, Bauteil2.D2
  N8: Alps_Motor-Slider.pin_1, Bauteil2.A+
  N9: Alps_Motor-Slider.pin_2, Bauteil2.A-
  N10: R5.leg1, Bauteil2.5V
  N11: R5.wiper, Bauteil2.A2
  N12: LED2.anode, Bauteil2.A5
  N13: Bauteil2.VMOT, Power_plug1.VCC

notes:
  Touch-Sensor
  220 Ohm
  1M Ohm
